# Fritzing sketch project  Sketch 2 (saved by Fritzing 0.9.6b)
breadboards: 1

parts:
  Mod1 = Raspberry Pi 4B
  Sensor1 = TTP223B Capacitive Touch Sensor Module
  Sensor2 = TTP223B Capacitive Touch Sensor Module
  Sensor3 = TTP223B Capacitive Touch Sensor Module
  Sensor4 = TTP223B Capacitive Touch Sensor Module
  Sensor5 = TTP223B Capacitive Touch Sensor Module
  Sensor6 = TTP223B Capacitive Touch Sensor Module
  Sensor7 = TTP223B Capacitive Touch Sensor Module
  Sensor8 = TTP223B Capacitive Touch Sensor Module
  Sensor9 = TTP223B Capacitive Touch Sensor Module
  LED1 = DUO LED RG [package="5 mm [THT]"]
  LED2 = DUO LED RG [package="5 mm [THT]"]
  LED3 = DUO LED RG [package="5 mm [THT]"]
  LED4 = DUO LED RG [package="5 mm [THT]"]
  LED5 = DUO LED RG [package="5 mm [THT]"]
  LED6 = DUO LED RG [package="5 mm [THT]"]
  LED7 = DUO LED RG [package="5 mm [THT]"]
  LED8 = DUO LED RG [package="5 mm [THT]"]
  LED9 = DUO LED RG [package="5 mm [THT]"]
  IC1 = MCP23017 I2C I/O Expander

nets:
  VCC: Mod1.5V, Sensor1.VCC, Sensor2.VCC, Sensor3.VCC, Sensor4.VCC, Sensor5.VCC, Sensor6.VCC, Sensor7.VCC, Sensor8.VCC, Sensor9.VCC
  N1: Mod1.GPIO4, Sensor9.SIG
  GND: Mod1.GND, Sensor1.GND, Sensor2.GND, Sensor3.GND, Sensor4.GND, Sensor5.GND, Sensor6.GND, Sensor7.GND, Sensor8.GND, Sensor9.GND, LED1.common_cathode, LED2.common_cathode, LED3.common_cathode, LED4.common_cathode, LED5.common_cathode, LED6.common_cathode, LED7.common_cathode, LED8.common_cathode, LED9.common_cathode
  N2: Sensor1.SIG, IC1.GPA0
  N3: Sensor2.SIG, IC1.GPA1
  N4: Sensor3.SIG, IC1.GPA2
  N5: Sensor4.SIG, IC1.GPA3
  N6: Sensor5.SIG, IC1.GPA4
  N7: Sensor6.SIG, IC1.GPA5
  N8: Sensor7.SIG, IC1.GPA6
  N9: Sensor8.SIG, IC1.GPA7

custom parts:
  TTP223B Capacitive Touch Sensor Module: The TTP223B capacitive touch sensor module uses the TTP223B IC. The appropriate voltage is approximately 2 to 5.5 volts.
  MCP23017 I2C I/O Expander: The MCP23017 uses two i2c pins (these can be shared with other i2c devices), and in exchange gives you 16 general purpose pins. You can set each of 16 pins to be input, output, input with a pullup or open drain. There's even the ability to get an interrupt via an external pin when any of the inputs change so you don't have to keep polling the chip.
